# Fritzing sketch Wiring Diagram (saved by Fritzing 0.9.4)
breadboards: 1

parts:
  U1 = NodeMCU V1.0
  microSD1 = MicroSD Card Module
  U2 = WS2812 RGB LED strip

nets:
  N1: U1.D2, U2.DIN
  GND: U1.GND, microSD1.GND, U2.GND
  N2: U1.D5, microSD1.SCK
  N3: U1.D6, microSD1.MISO
  N4: U1.D7, microSD1.MOSI
  N5: U1.D8, microSD1.CS
  VCC: U1.Vin, microSD1.VCC, U2.VCC

custom parts:
  NodeMCU V1.0: ESP8266 based NodeMCU
  WS2812 RGB LED strip: WS2812 strip
